# Fritzing sketch arduino-esp32-s2-ili9341-with-touchscreen (saved by Fritzing 0.9.9b)
breadboards: 1

parts:
  LCD1 = 2.8" SPI TFT Module [part_number=MSP2807]  # not connected
  M1 = ESP32-S2-DevKit [part_number=ESP32-S2-DevKit]

nets:
  N1: M1.G-21, M1.5V-42

custom parts:
  2.8" SPI TFT Module: A generic 2.8 inch LCD TFT 320x240 display with touchscreen and SD card slot. Uses the ILI9341 controller, like the Adafruit displays of this size uses.
  ESP32-S2-DevKit: The DOIT Esp32 DevKit v1 is one of the development board created by DOIT to evaluate the ESP-WROOM-32 module. It is based on the ESP32 microcontroller that boasts Wifi, Bluetooth, Ethernet and Low Power support all in a single chip. This module is 42pins long (2x21) and 11 pins width.
