# Fritzing sketch arduino-i2c-discovery (saved by Fritzing 0.9.9b)
breadboards: 1

parts:
  Part1 = GY-21P
  Squix1 = OLED 0.96" 128x64 I2C SSD1306
  U1 = NodeMCU V3.0

nets:
  VCC: Part1.VCC, Squix1.VCC, U1.3V3
  GND: Part1.GND, Squix1.GND, U1.GND#6, U1.GND#13, U1.GND#16, U1.GND#33
  N1: Part1.SCL, Squix1.SCL, U1.D2
  N2: Part1.SDA, Squix1.SCA, U1.D1

custom parts:
  GY-21P: The GY-21P module consists of two sensors, BMP280 and SI7021, which include pressure, temperature and humidity sensors. The communication protocol of this module is I2C. This module is capable of measuring air pressure from 30,000Pa to 110,000Pa, measuring humidity from 0 to 100%, measuring altitude from 0 to 30,000 feet and measuring temperature from -40 to +85 degrees Celsius. This sensor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
  NodeMCU V3.0: ESP8266 based NodeMCU
