# Fritzing sketch arduino_gy-21p (saved by Fritzing 0.9.9b)
breadboards: 1

parts:
  U1 = NodeMCU V3.0
  OLED2 = OLED 128x64 I2C Monochrome Display
  Part1 = Barometric Pressure Sensor - BMP180 Breakout (GY-68)

nets:
  N1: U1.D1, OLED2.SCK, Part1.SCL
  N2: U1.D2, OLED2.SDA, Part1.SDA
  3V3: U1.3V3, OLED2.VDD, Part1.VCC
  GND: U1.GND#6, U1.GND#13, U1.GND#16, U1.GND#33, OLED2.GND, Part1.GND

custom parts:
  NodeMCU V3.0: ESP8266 based NodeMCU
